# Fritzing sketch Schematic (saved by Fritzing 0.9.3b)

parts:
  Bauteil1 = Arduino Nano (Rev3.0)
  M1 = Dagu DGServo 9g (End View) [part_number=RS001B]
  S3 = Pushbutton [package="[THT]"]
  M2 = Dagu DGServo 9g (End View) [part_number=RS001B]

nets:
  GND: Bauteil1.GND, M1.gnd, S3.Pin_3, S3.Pin_4, M2.gnd
  N1: Bauteil1.D8, S3.Pin_1, S3.Pin_2
  N2: Bauteil1.D9, M1.pulse
  N3: Bauteil1.D10, M2.pulse
  VCC: Bauteil1.5V, M1.vcc, M2.vcc

notes:
  Servo for lower plate
  Servo for upper plate
